# Fritzing sketch Schaltplan Ampel (saved by Fritzing 0.9.3b)
breadboards: 1

parts:
  Arduino = Arduino Nano v2.3
  Car_Green = smd LED [color="Red (633nm)" package="0805 [SMD]"]
  Car_Yellow = smd LED [color="Red (633nm)" package="0805 [SMD]"]
  Car_Red = smd LED [color="Red (633nm)" package="0805 [SMD]"]
  Pass_Red = smd LED [color="Red (633nm)" package="0805 [SMD]"]
  Pass_Green = smd LED [color="Red (633nm)" package="0805 [SMD]"]
  R1 = Resistor [tolerance=±5% resistance=220 package=THT]
  R2 = Resistor [tolerance=±5% resistance=220 package=THT]
  R3 = Resistor [tolerance=±5% resistance=220 package=THT]
  R4 = Resistor [tolerance=±5% resistance=220 package=THT]
  R5 = Resistor [tolerance=±5% resistance=220 package=THT]
  S1 = Pushbutton [package="[THT]"]

nets:
  N1: Arduino.D5, S1.Pin_3, S1.Pin_4
  N2: Arduino.D7, R5.Pin_0
  N3: Arduino.D8, R4.Pin_0
  N4: Arduino.D9, R3.Pin_0
  N5: Arduino.D10, R2.Pin_0
  N6: Arduino.D11, R1.Pin_0
  N7: Arduino.GND, Car_Green.cathode, Car_Yellow.cathode, Car_Red.cathode, Pass_Red.cathode, Pass_Green.cathode, S1.Pin_1, S1.Pin_2
  N8: Car_Green.anode, R5.Pin_1
  N9: Car_Yellow.anode, R3.Pin_1
  N10: Car_Red.anode, R1.Pin_1
  N11: Pass_Red.anode, R2.Pin_1
  N12: Pass_Green.anode, R4.Pin_1
